# Fritzing sketch Breadboard (saved by Fritzing 0.9.10b)
breadboards: 1

parts:
  Mod2 = Amica NodeMCU DEVKIT 1.0
  Bauteil1 = 12 NeoPixel Ring [part_number=1643]  # not connected

nets:
  N1: Mod2.pin2, Mod2.pin_29
  N2: Mod2.pin_19, Mod2.pin_30

custom parts:
  12 NeoPixel Ring: 12 ultra bright smart LED NeoPixels are arranged in a circle with 1.5" (37mm) outer diameter. The rings are 'chainable' - connect the output pin of one to the input pin of another. Use only one microcontroller pin to control as many as you can chain together! Each LED is addressable as the driver chip is inside the LED. Each one has ~18mA constant current drive so the color will be very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
